// Logisim project s-mips.circ as structural Verilog
module S_MIPS_Board (
  input  DESHABILITAR_DISPATCHER,
  output halt
);

  wire button_1_out, CLK, CS, d_ff_1_q, LCLR, LoadRAM, LoadRAMOn, LW, R_R_W, R_W, ram_dispatcher_1_finished,
       RCS, Reset_out, RST, TTY_EN;
  wire [2:0] KDB;
  wire [3:0] LMask, Mask, ram_1_read_time, ram_1_write_time, RMask;
  wire [6:0] KDB_DATA, TTY_DATA;
  wire [15:0] Addr, LAddr, RAddr;
  wire [31:0] I0, I1, I2, I3, LData, ram_1_data_out_0, ram_1_data_out_1, ram_1_data_out_2, ram_1_data_out_3,
       RI0, RI1, RI2, RI3;

  TTY #(.rows(25), .cols(80)) tty_1 (.data(TTY_DATA), .clk(CLK), .we(TTY_EN), .clr(RST));
  not not_1 (LoadRAMOn, ram_dispatcher_1_finished);
  RAM_Dispatcher ram_dispatcher_1 (
    .WriteTime(ram_1_write_time), .Clock(CLK), .Data(LData), .Address(LAddr), .Mask(LMask),
    .Finished(ram_dispatcher_1_finished), .Write(LW), .CLR(LCLR));
  Keyboard #(.buflen(64)) keyboard_1 (.clk(CLK), .re(KDB[0]), .avail(KDB[2]), .data(KDB_DATA));  // open: clr
  RAM ram_1 (
    .Address(RAddr), .Data_Out_0(ram_1_data_out_0), .Data_Out_1(ram_1_data_out_1),
    .Data_Out_2(ram_1_data_out_2), .Data_Out_3(ram_1_data_out_3), .Data_In_0(RI0), .Data_In_1(RI1),
    .Data_In_2(RI2), .Data_In_3(RI3), .Mask(RMask), .nRead_Write(R_R_W), .Chip_Select(RCS),
    .Read_Time(ram_1_read_time), .Reset(button_1_out), .Write_Time(ram_1_write_time));
  Button button_1 (.out(button_1_out));
  D_Flip_Flop d_ff_1 (.clk(CLK), .D(1'b1), .Q(d_ff_1_q), .reset(Reset_out));  // open: Qn, preset, en
  Button Reset (.out(Reset_out));
  S_MIPS s_mips_1 (
    .Kbd_Enable(KDB[0]), .Address(Addr), .Kbd_Clear(KDB[1]), .Kbd_Available(KDB[2]), .RAM_In_0(I0),
    .Kbd_ASCII_Data(KDB_DATA), .RAM_In_1(I1), .TTY_Enable(TTY_EN), .RAM_In_2(I2), .RAM_In_3(I3),
    .TTY_ASCII_Data(TTY_DATA), .Reset(RST), .RAM_Out_0(ram_1_data_out_0), .Clock(CLK),
    .RAM_Out_1(ram_1_data_out_1), .Stop(halt), .RAM_Out_2(ram_1_data_out_2), .RAM_Out_3(ram_1_data_out_3),
    .Mask(Mask), .Read_Time(ram_1_read_time), .Write_Time(ram_1_write_time), .nRead_Write(R_W),
    .Chip_Select(CS));
  D_Flip_Flop d_ff_2 (.clk(CLK), .D(d_ff_1_q), .Qn(LCLR), .reset(Reset_out));  // open: Q, preset, en
  or or_1 (RST, LCLR, LoadRAM);
  Clock clock_1 (.out(CLK));
  Multiplexer #(.width(32), .enable("false")) multiplexer_1 (.in0(I0), .in1(LData), .out(RI0), .sel(LoadRAM));
  Multiplexer #(.width(32), .enable("false")) multiplexer_2 (.in0(I1), .in1(LData), .out(RI1), .sel(LoadRAM));
  Multiplexer #(.width(32), .enable("false")) multiplexer_3 (.in0(I2), .in1(LData), .out(RI2), .sel(LoadRAM));
  Multiplexer #(.width(32), .enable("false")) multiplexer_4 (.in0(I3), .in1(LData), .out(RI3), .sel(LoadRAM));
  and and_1 (LoadRAM, ~DESHABILITAR_DISPATCHER, LoadRAMOn);  // AND_Gate
  Multiplexer #(.width(16), .enable("false")) multiplexer_5 (.in0(Addr), .in1(LAddr), .out(RAddr), .sel(LoadRAM));
  Multiplexer #(.width(4), .enable("false")) multiplexer_6 (.in0(Mask), .in1(LMask), .out(RMask), .sel(LoadRAM));
  Multiplexer #(.enable("false")) multiplexer_7 (.in0(CS), .in1(LW), .out(RCS), .sel(LoadRAM));
  Multiplexer #(.enable("false")) multiplexer_8 (.in0(R_W), .in1(LW), .out(R_R_W), .sel(LoadRAM));

  // Notes on the sheet:
  //   NO MODIFICAR
  //   Keyboard
endmodule

module RAM (
  input  [15:0] Address,
  input  [31:0] Data_In_0,
  input  [31:0] Data_In_1,
  input  [31:0] Data_In_2,
  input  [31:0] Data_In_3,
  input  [3:0] Mask,
  input  nRead_Write,
  input  Chip_Select,
  input  Reset,
  output [31:0] Data_Out_0,
  output [31:0] Data_Out_1,
  output [31:0] Data_Out_2,
  output [31:0] Data_Out_3,
  output [3:0] Read_Time,
  output [3:0] Write_Time
);

  wire and_2_out, and_3_out, and_4_out, and_5_out, and_6_out, and_7_out, and_8_out, and_9_out, Changed, CLK,
       comparator_2_eq, comparator_3_eq, comparator_4_eq, comparator_5_eq, comparator_6_eq, Count,
       demultiplexer_3_out0, Idle, Idle_q, Load, Load0, Load1, nand_1_out, or_1_out, or_2_out, or_3_out,
       or_4_out, or_5_out, or_6_out, or_7_out, or_8_out, or_9_out, or_10_out, Proc_q, Update_Mem, Zero_Time;
  wire [3:0] counter_1_q, multiplexer_1_out, subtractor_1_out;
  wire [31:0] register_1_q, register_2_q, register_3_q, register_4_q, register_5_q;

  // Probe on 4'b0011
  // Probe on 4'b0010
  Multiplexer #(.width(4), .enable("false")) multiplexer_1 (
    .in0(4'b0011), .in1(4'b0010), .out(multiplexer_1_out), .sel(nRead_Write));
  or or_1 (or_1_out, Idle, Update_Mem);
  or or_2 (or_2_out, ~Chip_Select, Reset);  // OR_Gate
  Subtractor #(.width(4)) subtractor_1 (.a(multiplexer_1_out), .b(4'b0010), .out(subtractor_1_out));  // open: bin, bout
  D_Flip_Flop u_Idle (.clk(CLK), .D(or_1_out), .Q(Idle_q), .preset(or_2_out));  // open: Qn, en, reset
  Demultiplexer #(.enable("false")) demultiplexer_1 (.out0(Idle), .out1(Load0), .in(Idle_q), .sel(Changed));
  // Probe on counter_1_q
  Counter #(.width(4), .max('hf)) counter_1 (
    .load(Load), .D(subtractor_1_out), .count(Count), .Q(counter_1_q), .clk(CLK), .clr(or_3_out));  // open: carry
  or or_3 (or_3_out, ~Chip_Select, Reset);  // OR_Gate
  Comparator #(.width(4), .mode("unsigned")) comparator_1 (
    .a(4'b0000), .b(counter_1_q), .eq(Zero_Time));  // open: gt, lt
  or or_4 (or_4_out, Count, Load0, Load1);
  Register #(.width(32)) register_1 (.D(Data_In_0), .en(Chip_Select), .Q(register_1_q), .clk(CLK), .clr(or_5_out));
  or or_5 (or_5_out, ~Chip_Select, Reset);  // OR_Gate
  Register #(.width(32)) register_2 (.D(Data_In_1), .en(Chip_Select), .Q(register_2_q), .clk(CLK), .clr(or_6_out));
  or or_6 (or_6_out, ~Chip_Select, Reset);  // OR_Gate
  Register #(.width(32)) register_3 (.D(Data_In_2), .en(Chip_Select), .Q(register_3_q), .clk(CLK), .clr(or_7_out));
  or or_7 (or_7_out, ~Chip_Select, Reset);  // OR_Gate
  Register #(.width(32)) register_4 (.D(Data_In_3), .en(Chip_Select), .Q(register_4_q), .clk(CLK), .clr(or_8_out));
  or or_8 (or_8_out, ~Chip_Select, Reset);  // OR_Gate
  Register #(.width(32)) register_5 (
    .D({{11{1'b1}}, nRead_Write, Mask, Address}), .en(Chip_Select), .Q(register_5_q), .clk(CLK),
    .clr(or_9_out));
  or or_9 (or_9_out, ~Chip_Select, Reset);  // OR_Gate
  D_Flip_Flop Proc (.clk(CLK), .D(or_4_out), .Q(Proc_q), .reset(or_10_out));  // open: Qn, preset, en
  or or_10 (or_10_out, ~Chip_Select, Reset);  // OR_Gate
  Demultiplexer #(.enable("false")) demultiplexer_2 (
    .out0(Count), .out1(Update_Mem), .in(demultiplexer_3_out0), .sel(Zero_Time));
  Demultiplexer #(.enable("false")) demultiplexer_3 (
    .out0(demultiplexer_3_out0), .out1(Load1), .in(Proc_q), .sel(Changed));
  Clock clock_1 (.out(CLK));
  Comparator #(.width(32)) comparator_2 (.a(register_1_q), .b(Data_In_0), .eq(comparator_2_eq));  // open: gt, lt
  Comparator #(.width(32)) comparator_3 (.a(register_2_q), .b(Data_In_1), .eq(comparator_3_eq));  // open: gt, lt
  Comparator #(.width(32)) comparator_4 (.a(register_3_q), .b(Data_In_2), .eq(comparator_4_eq));  // open: gt, lt
  Comparator #(.width(32)) comparator_5 (.a(register_4_q), .b(Data_In_3), .eq(comparator_5_eq));  // open: gt, lt
  Comparator #(.width(32)) comparator_6 (
    .a(register_5_q), .b({{11{1'b1}}, nRead_Write, Mask, Address}), .eq(comparator_6_eq));  // open: gt, lt
  nand nand_1 (nand_1_out, comparator_6_eq, comparator_2_eq, comparator_3_eq, comparator_4_eq, comparator_5_eq);
  and and_1 (Changed, nand_1_out, Chip_Select);
  or or_11 (Load, Count, Load1, Load0);
  and and_2 (and_2_out, Mask[0], Update_Mem, nRead_Write);
  and and_3 (and_3_out, Mask[1], Update_Mem, nRead_Write);
  and and_4 (and_4_out, Mask[2], Update_Mem, nRead_Write);
  and and_5 (and_5_out, Mask[3], Update_Mem, nRead_Write);
  RAM_part #(.addrWidth(16), .dataWidth(32), .bus("separate")) ram_1 (
    .addr(Address), .din(Data_In_0), .data(Data_Out_0), .str(and_2_out), .sel(Chip_Select), .clk(CLK),
    .ld(and_6_out), .clr(Reset));
  and and_6 (and_6_out, ~nRead_Write, Idle);  // AND_Gate
  RAM_part #(.addrWidth(16), .dataWidth(32), .bus("separate")) ram_2 (
    .addr(Address), .din(Data_In_1), .data(Data_Out_1), .str(and_3_out), .sel(Chip_Select), .clk(CLK),
    .ld(and_7_out), .clr(Reset));
  and and_7 (and_7_out, ~nRead_Write, Idle);  // AND_Gate
  RAM_part #(.addrWidth(16), .dataWidth(32), .bus("separate")) ram_3 (
    .addr(Address), .din(Data_In_2), .data(Data_Out_2), .str(and_4_out), .sel(Chip_Select), .clk(CLK),
    .ld(and_8_out), .clr(Reset));
  and and_8 (and_8_out, ~nRead_Write, Idle);  // AND_Gate
  RAM_part #(.addrWidth(16), .dataWidth(32), .bus("separate")) ram_4 (
    .addr(Address), .din(Data_In_3), .data(Data_Out_3), .str(and_5_out), .sel(Chip_Select), .clk(CLK),
    .ld(and_9_out), .clr(Reset));
  and and_9 (and_9_out, ~nRead_Write, Idle);  // AND_Gate

  assign Read_Time = 4'b0011;
  assign Write_Time = 4'b0010;

  // Other names for the same wires on the sheet: M0 = Mask[0]; M1 = Mask[1]; M2 = Mask[2]; M3 = Mask[3];
  //   RW = nRead_Write; CLR = Reset; CS = Chip_Select; Load2 = Count

  // Notes on the sheet:
  //   NO MODIFICAR
  //   excepto quizás los valores RT y WT
  //   BANK0
  //   BANK1
  //   BANK2
  //   BANK3
endmodule

module RAM_Dispatcher (
  input  [3:0] WriteTime,
  input  Clock,
  input  CLR,
  output [31:0] Data,
  output [15:0] Address,
  output [3:0] Mask,
  output Finished,
  output Write
);

  wire demultiplexer_2_out1, demultiplexer_3_out1, End, IDLE_q, IncAddr, Load, or_1_out, or_2_out, While_q,
       WriteEnd;
  wire [3:0] counter_1_q;
  wire [31:0] CurrentAddress_q;

  Counter #(.width(32), .max('hffffffff)) CurrentAddress (
    .count(IncAddr), .Q({CurrentAddress_q[31:18], Address, CurrentAddress_q[1:0]}), .clk(Clock), .clr(CLR));  // open: load, D, carry
  or or_1 (or_1_out, IncAddr, demultiplexer_3_out1, Finished);
  D_Flip_Flop IDLE (.clk(Clock), .D(or_1_out), .Q(IDLE_q), .preset(CLR));  // open: Qn, en, reset
  Demultiplexer #(.enable("false")) demultiplexer_1 (.out0(Load), .out1(Finished), .in(IDLE_q), .sel(End));
  D_Flip_Flop While (.clk(Clock), .D(or_2_out), .Q(While_q), .reset(CLR));  // open: Qn, preset, en
  or or_2 (or_2_out, Write, Load);
  RAM_part #(.addrWidth(18), .dataWidth(32)) ram_1 (
    .addr({Address, CurrentAddress_q[1:0]}), .data(Data), .clk(Clock));  // open: sel, ld, clr
  Demultiplexer #(.enable("false")) demultiplexer_2 (
    .out0(Write), .out1(demultiplexer_2_out1), .in(While_q), .sel(WriteEnd));
  Decoder #(.select(2)) decoder_1 (
    .out0(Mask[0]), .out1(Mask[1]), .out2(Mask[2]), .out3(Mask[3]), .sel(CurrentAddress_q[1:0]));  // open: en
  Demultiplexer #(.enable("false")) demultiplexer_3 (
    .out0(IncAddr), .out1(demultiplexer_3_out1), .in(demultiplexer_2_out1), .sel(End));
  Counter #(.width(4), .max('hf)) counter_1 (
    .load(Load), .D(WriteTime), .count(Write), .Q(counter_1_q), .clk(Clock));  // open: carry, clr
  Comparator #(.width(32)) comparator_1 (.a(Data), .b({32{1'b1}}), .eq(End));  // open: gt, lt
  Comparator #(.width(4)) comparator_2 (.a(4'b0000), .b(counter_1_q), .eq(WriteEnd));  // open: gt, lt

  // Other names for the same wires on the sheet: CLK = Clock; Count = Write; WT[3:0] = WriteTime
endmodule

module S_MIPS (
  input  Kbd_Available,
  input  [6:0] Kbd_ASCII_Data,
  input  [31:0] RAM_Out_0,
  input  [31:0] RAM_Out_1,
  input  Reset,
  input  [31:0] RAM_Out_2,
  input  Clock,
  input  [31:0] RAM_Out_3,
  input  [3:0] Read_Time,
  input  [3:0] Write_Time,
  output Kbd_Enable,
  output [15:0] Address,
  output Kbd_Clear,
  output TTY_Enable,
  output [6:0] TTY_ASCII_Data,
  output Stop,
  output [31:0] RAM_In_0,
  output [31:0] RAM_In_1,
  output [31:0] RAM_In_2,
  output [31:0] RAM_In_3,
  output [3:0] Mask,
  output nRead_Write,
  output Chip_Select
);

  wire data_path_1_tty, HALT, LOADING_INST, PC, PC_ADDRESS, RAM_INST, RAM_READ, WRITE_RAM;
  wire [6:0] KBD_DATA_t;
  wire [31:0] DATA, MEMORY, RAM_DATA;

  CONTROL_UNIT control_unit_1 (
    .CLK(Clock), .WRITE(WRITE_RAM), .RST(Reset), .PC(PC), .HALT(HALT), .RAM_INST(RAM_INST),
    .R_TIME(Read_Time), .W_TIME(Write_Time), .STOP(Stop), .CS(Chip_Select), .WRITE_2(nRead_Write),
    .PC_ADDRESS(PC_ADDRESS), .RAM_READ(RAM_READ), .LOADING_INST(LOADING_INST));
  WRITE_RAM write_ram_1 (
    .ADDRESS(Address), .VALUE(RAM_DATA), .MASK(Mask), .INPUT0(RAM_In_0), .INPUT1(RAM_In_1),
    .INPUT2(RAM_In_2), .INPUT3(RAM_In_3), .MEMORY(MEMORY));
  READ_RAM read_ram_1 (
    .BANK0(RAM_Out_0), .BANK1(RAM_Out_1), .BANK2(RAM_Out_2), .BANK3(RAM_Out_3), .MEMORY(MEMORY),
    .RAM_DATA(DATA));
  Data_Path data_path_1 (
    .RST(Reset), .CLK(Clock), .EN_PC(PC), .INSTRUCTION(DATA), .KEYBOARD(KBD_DATA_t),
    .load_inst(LOADING_INST), .RAM_READ(RAM_READ), .PC_LOAD(PC_ADDRESS), .MEMORY(MEMORY),
    .MEMORY_INST(RAM_INST), .WRITE_RAM(WRITE_RAM), .TTY_DATA(TTY_ASCII_Data), .KBD(Kbd_Enable),
    .RAM_DATA(RAM_DATA), .TTY(data_path_1_tty), .HALT(HALT));
  and and_1 (TTY_Enable, data_path_1_tty, PC);

  assign Kbd_Clear = Reset;

  // Other names for the same wires on the sheet: CLK = Clock; CS = Chip_Select; KBD_AVAIL = Kbd_Available;
  //   CLR = Reset; KBD_CLR = Reset; KBD_DATA[6:0] = Kbd_ASCII_Data; RAM_A[15:0] = Address;
  //   RAM_INPUT_0[31:0] = RAM_In_0; RAM_INPUT_1[31:0] = RAM_In_1; RAM_INPUT_2[31:0] = RAM_In_2;
  //   RAM_INPUT_3[31:0] = RAM_In_3; RAM_MASK[3:0] = Mask; RAM_OUTPUT_0[31:0] = RAM_Out_0;
  //   RAM_OUTPUT_1[31:0] = RAM_Out_1; RAM_OUTPUT_2[31:0] = RAM_Out_2; RAM_OUTPUT_3[31:0] = RAM_Out_3;
  //   RW = nRead_Write; TTY_DATA[6:0] = TTY_ASCII_Data

  // Notes on the sheet:
  //   RAM ADDRESS
  //   DATA FROM RAM
  //   DATA TO RAM
  //   DATA WRITE MASK
  //   RAM TIMING
  //   RAM CONTROL
  //   KEYBOARD
  //   TTY
  //   SEQUENCING
endmodule

module Data_Path (
  input  RST,
  input  CLK,
  input  EN_PC,
  input  [31:0] INSTRUCTION,
  input  [6:0] KEYBOARD,
  input  load_inst,
  input  RAM_READ,
  input  PC_LOAD,
  output [31:0] MEMORY,
  output MEMORY_INST,
  output WRITE_RAM,
  output [6:0] TTY_DATA,
  output KBD,
  output [31:0] RAM_DATA,
  output TTY,
  output HALT
);

  wire ADD, ADDI, AND, and_1_out, and_2_out, ANDI, BEQ, BGTZ, BLEZ, BLTZ, BNE, DIV, DIVU, J, JR, LW, MFHI,
       MFLO, MULT, MULU, NF, NOP, NOR, OR, or_1_out, or_2_out, or_3_out, or_4_out, ORI, POP, PUSH, RND, SLT,
       SLTI, SLTIU, SLTU, SUB, SW, TYPE_I, Write, XOR, XORI, ZF;
  wire [3:0] ALU_SELECTOR;
  wire [4:0] multiplexer_1_out, Rd, Rs, Rt;
  wire [15:0] CONST;
  wire [25:0] DESTINO_SALTO;
  wire [31:0] ALU_OUTPUT, BC_OUT, bit_extender_1_out, bit_extender_2_out, HI, LO, multiplexer_2_out,
       multiplexer_3_out, PC, register_1_q, register_file_input_1_output, RND_GENERATOR, RT_t, SP;
  wire [31:7] RS_t;

  // Probe on RND_GENERATOR
  Random #(.width(32)) random_1 (.clk(CLK), .next(RND), .out(RND_GENERATOR));  // open: clr
  Register #(.width(32)) register_1 (.D(INSTRUCTION), .en(load_inst), .Q(register_1_q), .clk(CLK), .clr(RST));
  REGISTER_FILE_INPUT register_file_input_1 (
    .KEYBOARD(KEYBOARD), .ALU(ALU_OUTPUT), .RND(RND_GENERATOR), .MEMORY(INSTRUCTION), .HIGH(HI), .LOW(LO),
    .LW(LW), .POP(POP), .MFHI(MFHI), .MFLO(MFLO), .isKBD(KBD), .isRND(RND),
    .Output(register_file_input_1_output));
  Multiplexer #(.width(5), .enable("false")) multiplexer_1 (.in0(Rd), .in1(Rt), .out(multiplexer_1_out), .sel(TYPE_I));
  Instruction_Decoder instruction_decoder_1 (
    .Instruction(register_1_q), .ADD(ADD), .AND(AND), .SLT(SLT), .NOP(NOP), .LW(LW), .SUB(SUB), .OR(OR),
    .SLTU(SLTU), .BEQ(BEQ), .SW(SW), .MULT(MULT), .NOR(NOR), .SLTI(SLTI), .BNE(BNE), .POP(POP), .MULU(MULU),
    .XOR(XOR), .SLTIU(SLTIU), .BLEZ(BLEZ), .PUSH(PUSH), .DIV(DIV), .ANDI(ANDI), .BGTZ(BGTZ), .DIVU(DIVU),
    .ORI(ORI), .MFHI(MFHI), .BLTZ(BLTZ), .HALT(HALT), .ADDI(ADDI), .XORI(XORI), .MFLO(MFLO), .J(J),
    .TTY(TTY), .JR(JR), .RND(RND), .KBD(KBD), .Constante(CONST), .Destino_Salto(DESTINO_SALTO), .Rs(Rs),
    .Rt(Rt), .Rd(Rd));
  Register_File register_file_1 (
    .DA(multiplexer_1_out), .DI(register_file_input_1_output), .Clk(CLK), .Reset(RST), .R_W(Write), .SA(Rs),
    .SB(Rt), .B(RT_t), .A({RS_t, TTY_DATA}), .PUSH(PUSH), .POP(POP), .EN_PC(EN_PC), .STACK_POINTER(SP));  // open: Mult_or_Div, Hi_Input, Lo_Input, Hi_Output, Lo_Output
  or or_1 (or_1_out, ADD, AND, ORI, SUB, OR, XORI, RND, NOR, MFHI, XOR, MFLO, ADDI, KBD, SLTI, SLT, SLTIU, SLTU, ANDI);
  or or_2 (or_2_out, SW, ADDI, LW);
  or or_3 (or_3_out, POP, LW);
  assign bit_extender_1_out = {{16{CONST[15]}}, CONST};  // Bit_Extender bit_extender_1
  assign bit_extender_2_out = {{16{1'b0}}, CONST};  // Bit_Extender bit_extender_2
  and and_1 (and_1_out, EN_PC, or_1_out);
  and and_2 (and_2_out, or_3_out, RAM_READ);
  // Probe on bit_extender_1_out
  Multiplexer #(.width(32), .enable("false")) multiplexer_2 (
    .in0(bit_extender_1_out), .in1(bit_extender_2_out), .out(multiplexer_2_out), .sel(or_4_out));
  or or_4 (or_4_out, ANDI, ORI, XORI);
  or or_5 (Write, and_1_out, and_2_out);
  ALU_Encoder alu_encoder_1 (
    .ADD(ADD), .ADDI(or_2_out), .SUB(SUB), .MULT(MULT), .MULU(MULU), .DIV(DIV), .DIVU(DIVU), .SLT(SLT),
    .SLTI(SLTI), .SLTU(SLTU), .SLTIU(SLTIU), .AND(AND), .ANDI(ANDI), .OR(OR), .ORI(ORI), .XOR(XOR),
    .XORI(XORI), .NOR(NOR), .TYPE_I(TYPE_I), .ALU_SELECTOR(ALU_SELECTOR));
  Multiplexer #(.width(32), .enable("false")) multiplexer_3 (
    .in0(RT_t), .in1(multiplexer_2_out), .out(multiplexer_3_out), .sel(TYPE_I));
  ALU alu_1 (
    .Operator_A({RS_t, TTY_DATA}), .Operator_B(multiplexer_3_out), .Selector(ALU_SELECTOR),
    .Output(ALU_OUTPUT), .Zero(ZF), .Neg(NF), .CLK(CLK), .HIGH(HI), .LOW(LO));
  Branch_Control branch_control_1 (
    .NOP(NOP), .BEQ(BEQ), .DEST(DESTINO_SALTO), .RS({RS_t, TTY_DATA}), .RT(RT_t), .PC(PC), .BNE(BNE),
    .OFFSET(CONST), .BLEZ(BLEZ), .BGTZ(BGTZ), .BLTZ(BLTZ), .JR(JR), .J(J), .BC_OUT(BC_OUT));
  Program_Counter program_counter_1 (.ENABLE(EN_PC), .PC_OUTPUT(PC), .RESET(RST), .INPUT(BC_OUT), .CLK(CLK));
  Memory_Address memory_address_1 (
    .ALU(ALU_OUTPUT), .PC(PC), .SP(SP), .POP(POP), .PUSH(PUSH), .LW(LW), .SW(SW), .PC_ADDRESS(PC_LOAD),
    .MEMORY(MEMORY));
  or or_6 (WRITE_RAM, SW, PUSH);
  Multiplexer #(.width(32), .enable("false")) multiplexer_4 (
    .in0({RS_t, TTY_DATA}), .in1(RT_t), .out(RAM_DATA), .sel(SW));
  or or_7 (MEMORY_INST, LW, WRITE_RAM, POP);

  // Other names for the same wires on the sheet: INST[31:0] = INSTRUCTION; RS_t[6:0] = TTY_DATA

  // Notes on the sheet:
  //   DataPath
endmodule

module CONTROL_UNIT (
  input  CLK,
  input  WRITE,
  input  RST,
  input  HALT,
  input  RAM_INST,
  input  [3:0] R_TIME,
  input  [3:0] W_TIME,
  output PC,
  output LOADING_INST,
  output STOP,
  output CS,
  output RAM_READ,
  output WRITE_2,
  output PC_ADDRESS
);

  wire CHIP1, CHIP2, demultiplexer_1_out1, demultiplexer_2_out0, demultiplexer_3_out0, demultiplexer_4_out0,
       demultiplexer_5_out0, IDLE_q, LOADING_q, or_2_out, or_3_out, or_4_out, or_7_out, RAM, RAM_READ_t,
       STOP_t, TIMER_RESET, WAIT_RAM, WAIT_READ;
  wire [3:0] multiplexer_1_out;

  Multiplexer #(.width(4), .enable("false")) multiplexer_1 (
    .in0(R_TIME), .in1(W_TIME), .out(multiplexer_1_out), .sel(WRITE));
  or or_1 (PC, demultiplexer_5_out0, RAM_READ_t);
  or or_2 (or_2_out, demultiplexer_5_out0, RAM_READ_t, demultiplexer_1_out1);
  D_Flip_Flop RAM_WAITER (.clk(CLK), .D(or_3_out), .Q(CHIP2), .reset(RST));  // open: Qn, preset, en
  or or_3 (or_3_out, demultiplexer_2_out0, RAM);
  Demultiplexer #(.enable("false")) demultiplexer_1 (
    .out0(TIMER_RESET), .out1(demultiplexer_1_out1), .in(IDLE_q), .sel(RST));
  D_Flip_Flop IDLE (.clk(CLK), .D(or_2_out), .Q(IDLE_q), .preset(RST));  // open: Qn, en, reset
  Demultiplexer #(.enable("false")) demultiplexer_2 (
    .out0(demultiplexer_2_out0), .out1(RAM_READ), .in(CHIP2), .sel(WAIT_RAM));
  COUNTER counter_1 (.START(1'b1), .OUT(WAIT_RAM), .TIME(multiplexer_1_out), .CLK(CLK), .RESET(RAM));
  D_Flip_Flop LOADING___X2 (.clk(CLK), .D(RAM_READ), .Q(RAM_READ_t), .reset(RST));  // open: Qn, preset, en
  or or_4 (or_4_out, demultiplexer_3_out0, TIMER_RESET);
  D_Flip_Flop READ_WAITER (.clk(CLK), .D(or_4_out), .Q(CHIP1), .reset(RST));  // open: Qn, preset, en
  or or_5 (PC_ADDRESS, CHIP1, TIMER_RESET, PC);
  Demultiplexer #(.enable("false")) demultiplexer_3 (
    .out0(demultiplexer_3_out0), .out1(LOADING_INST), .in(CHIP1), .sel(WAIT_READ));
  or or_6 (CS, CHIP1, CHIP2);
  and and_1 (WRITE_2, CHIP2, WRITE);
  Demultiplexer #(.enable("false")) demultiplexer_4 (
    .out0(demultiplexer_4_out0), .out1(STOP_t), .in(LOADING_q), .sel(HALT));
  D_Flip_Flop LOADING (.clk(CLK), .D(LOADING_INST), .Q(LOADING_q), .reset(RST));  // open: Qn, preset, en
  or or_7 (or_7_out, STOP, STOP_t);
  COUNTER counter_2 (.START(1'b1), .OUT(WAIT_READ), .TIME(R_TIME), .CLK(CLK), .RESET(TIMER_RESET));
  Demultiplexer #(.enable("false")) demultiplexer_5 (
    .out0(demultiplexer_5_out0), .out1(RAM), .in(demultiplexer_4_out0), .sel(RAM_INST));
  D_Flip_Flop u_HALT (.clk(CLK), .D(or_7_out), .Q(STOP), .reset(RST));  // open: Qn, preset, en

  // Other names for the same wires on the sheet: RAM_RESET = RAM

  // Notes on the sheet:
  //   INPUT
  //   CONTROL_UNIT
endmodule

module READ_RAM (
  input  [31:0] BANK0,
  input  [31:0] BANK1,
  input  [31:0] BANK2,
  input  [31:0] BANK3,
  input  [31:0] MEMORY,
  output [31:0] RAM_DATA
);

  Multiplexer #(.select(2), .width(32), .enable("false")) multiplexer_1 (
    .in0(BANK0), .in1(BANK1), .in2(BANK2), .in3(BANK3), .out(RAM_DATA), .sel(MEMORY[3:2]));

  // Other names for the same wires on the sheet: SELECTOR[1:0] = MEMORY[3:2]
endmodule

module WRITE_RAM (
  input  [31:0] MEMORY,
  input  [31:0] VALUE,
  output [3:0] MASK,
  output [15:0] ADDRESS,
  output [31:0] INPUT0,
  output [31:0] INPUT1,
  output [31:0] INPUT2,
  output [31:0] INPUT3
);

  Demultiplexer #(.select(2), .enable("false")) demultiplexer_1 (
    .out0(MASK[0]), .out1(MASK[1]), .out2(MASK[2]), .out3(MASK[3]), .in(1'b1), .sel(MEMORY[3:2]));
  Demultiplexer #(.select(2), .width(32), .enable("false")) demultiplexer_2 (
    .out0(INPUT0), .out1(INPUT1), .out2(INPUT2), .out3(INPUT3), .in(VALUE), .sel(MEMORY[3:2]));

  assign ADDRESS = MEMORY[19:4];

  // Other names for the same wires on the sheet: SELECTOR[1:0] = MEMORY[3:2]

  // Notes on the sheet:
  //   LITTLE_ENDIAN A BIG-ENDIAN ????
endmodule

module ALU (
  input  [31:0] Operator_A,
  input  [31:0] Operator_B,
  input  [3:0] Selector,
  input  CLK,
  output [31:0] HIGH,
  output [31:0] Output,
  output [31:0] LOW,
  output Zero,
  output Neg
);

  wire comparator_1_lt, comparator_2_lt, ENABLE_HIGH_LOW;
  wire [1:0] SELECTOR_MUL_DIV;
  wire [31:0] ADD, AND, divider_1_out, divider_1_rem, division_1_hi, division_1_lo, multiplexer_2_out,
       multiplexer_3_out, multiplication_1_hi, multiplication_1_lo, multiplier_1_cout, multiplier_1_out, NOR,
       OR, SLT, SLTU, SUB, XOR;

  assign AND = Operator_A & Operator_B;  // AND_Gate and_1, 32 bits wide
  assign OR = Operator_A | Operator_B;  // OR_Gate or_1, 32 bits wide
  assign NOR = ~(Operator_A | Operator_B);  // NOR_Gate nor_1, 32 bits wide
  assign XOR = Operator_A ^ Operator_B;  // XOR_Gate xor_1, 32 bits wide
  Comparator #(.width(32)) comparator_1 (.a(Operator_A), .b(Operator_B), .lt(comparator_1_lt));  // open: gt, eq
  Comparator #(.width(32), .mode("unsigned")) comparator_2 (
    .a(Operator_A), .b(Operator_B), .lt(comparator_2_lt));  // open: gt, eq
  // Probe on comparator_2_lt
  // Probe on Operator_A
  // Probe on Operator_B
  // Probe on comparator_1_lt
  assign SLTU = {{31{1'b0}}, comparator_2_lt};  // Bit_Extender bit_extender_1
  assign SLT = {{31{1'b0}}, comparator_1_lt};  // Bit_Extender bit_extender_2
  // Probe on SLT
  Adder #(.width(32)) adder_1 (.a(Operator_A), .b(Operator_B), .out(ADD));  // open: cin, cout
  Subtractor #(.width(32)) subtractor_1 (.a(Operator_A), .b(Operator_B), .out(SUB));  // open: bin, bout
  // Probe on SLTU
  Multiplexer #(.select(4), .width(32), .enable("false")) multiplexer_1 (
    .in0(AND), .in1(OR), .in2(NOR), .in3(XOR), .in4(SLT), .in5(SLTU), .in6(ADD), .in7(SUB), .out(Output),
    .sel(Selector));  // open: in8, in9, in10, in11, in12, in13, in14, in15
  // Probe on Output
  Division division_1 (.A(Operator_A), .HI(division_1_hi), .LO(division_1_lo), .B(Operator_B));
  Multiplication multiplication_1 (.A(Operator_A), .HI(multiplication_1_hi), .B(Operator_B), .LO(multiplication_1_lo));
  Multiplier #(.width(32)) multiplier_1 (
    .a(Operator_A), .b(Operator_B), .out(multiplier_1_out), .cout(multiplier_1_cout));  // open: cin
  Divider #(.width(32)) divider_1 (
    .a(Operator_A), .b(Operator_B), .out(divider_1_out), .rem(divider_1_rem));  // open: upper
  Comparator #(.width(32)) comparator_3 (.a(Output), .b({32{1'b0}}), .eq(Zero), .lt(Neg));  // open: gt
  Multiplexer #(.select(2), .width(32), .enable("false")) multiplexer_2 (
    .in0(multiplier_1_cout), .in1(divider_1_rem), .in2(division_1_hi), .in3(multiplication_1_hi),
    .out(multiplexer_2_out), .sel(SELECTOR_MUL_DIV));
  Multiplexer #(.select(2), .width(32), .enable("false")) multiplexer_3 (
    .in0(multiplier_1_out), .in1(divider_1_out), .in2(division_1_lo), .in3(multiplication_1_lo),
    .out(multiplexer_3_out), .sel(SELECTOR_MUL_DIV));
  and and_2 (ENABLE_HIGH_LOW, Selector[3], ~Selector[2]);  // AND_Gate
  and and_3 (SELECTOR_MUL_DIV[1], Selector[3], ~Selector[2], Selector[1]);  // AND_Gate
  and and_4 (SELECTOR_MUL_DIV[0], Selector[3], ~Selector[2], Selector[0]);  // AND_Gate
  Register #(.width(32)) register_1 (.D(multiplexer_2_out), .en(ENABLE_HIGH_LOW), .Q(HIGH), .clk(CLK));  // open: clr
  Register #(.width(32)) register_2 (.D(multiplexer_3_out), .en(ENABLE_HIGH_LOW), .Q(LOW), .clk(CLK));  // open: clr

  // Other names for the same wires on the sheet: A[31:0] = Operator_A; B[31:0] = Operator_B; Selec[3:0] = Selector

  // Notes on the sheet:
  //   Inputs
  //   ALU
  //   FLAGS
endmodule

module ALU_Encoder (
  input  ADD,
  input  ADDI,
  input  SUB,
  input  MULT,
  input  MULU,
  input  DIV,
  input  DIVU,
  input  SLT,
  input  SLTI,
  input  SLTU,
  input  SLTIU,
  input  AND,
  input  ANDI,
  input  OR,
  input  ORI,
  input  XOR,
  input  XORI,
  input  NOR,
  output TYPE_I,
  output [3:0] ALU_SELECTOR
);

  wire ADD_t, AND_t, OR_t, SLT_t, SLTU_t, XOR_t;

  or or_1 (ADD_t, ADD, ADDI);
  or or_2 (SLT_t, SLT, SLTI);
  or or_3 (SLTU_t, SLTU, SLTIU);
  or or_4 (AND_t, AND, ANDI);
  or or_5 (OR_t, OR, ORI);
  or or_6 (XOR_t, XOR, XORI);
  or or_7 (TYPE_I, ADDI, SLTI, SLTIU, ANDI, ORI, XORI);
  or or_8 (ALU_SELECTOR[3], MULT, DIVU, DIV, MULU);
  or or_9 (ALU_SELECTOR[2], SLT_t, SLTU_t, ADD_t, SUB);
  or or_10 (ALU_SELECTOR[1], NOR, XOR_t, ADD_t, SUB, DIV, MULU);
  or or_11 (ALU_SELECTOR[0], OR_t, XOR_t, SLTU_t, SUB, DIVU, MULU);

  // Notes on the sheet:
  //   ALU_Encoder
endmodule

module Multiplication (
  input  [31:0] A,
  input  [31:0] B,
  output [31:0] HI,
  output [31:0] LO
);

  wire [31:0] adder_2_out, multiplexer_1_out, multiplexer_2_out, multiplier_1_cout;

  Multiplexer #(.width(32), .enable("false")) multiplexer_1 (
    .in0({32{1'b0}}), .in1(A), .out(multiplexer_1_out), .sel(B[31]));
  Multiplexer #(.width(32), .enable("false")) multiplexer_2 (
    .in0({32{1'b0}}), .in1(B), .out(multiplexer_2_out), .sel(A[31]));
  // Probe on LO
  Multiplier #(.width(32)) multiplier_1 (.a(A), .b(B), .out(LO), .cout(multiplier_1_cout));  // open: cin
  Adder #(.width(32)) adder_1 (.a(multiplier_1_cout), .b(adder_2_out), .out(HI));  // open: cin, cout
  Adder #(.width(32)) adder_2 (.a(multiplexer_1_out), .b(multiplexer_2_out), .out(adder_2_out));  // open: cin, cout
  // Probe on LO

  // Notes on the sheet:
  //   Unsigned_Multiplication
endmodule

module Division (
  input  [31:0] A,
  input  [31:0] B,
  output [31:0] HI,
  output [31:0] LO
);

  wire xor_1_out;
  wire [31:0] divider_1_out, multiplexer_1_out, multiplexer_2_out, negator_1_out, negator_2_out,
       negator_3_out;

  Multiplexer #(.width(32), .enable("false")) multiplexer_1 (
    .in0(A), .in1(negator_1_out), .out(multiplexer_1_out), .sel(A[31]));
  Negator #(.width(32)) negator_1 (.in(A), .out(negator_1_out));
  Multiplexer #(.width(32), .enable("false")) multiplexer_2 (
    .in0(B), .in1(negator_2_out), .out(multiplexer_2_out), .sel(B[31]));
  Negator #(.width(32)) negator_2 (.in(B), .out(negator_2_out));
  Divider #(.width(32)) divider_1 (
    .a(multiplexer_1_out), .b(multiplexer_2_out), .out(divider_1_out), .rem(HI));  // open: upper
  xor xor_1 (xor_1_out, A[31], B[31]);
  Multiplexer #(.width(32), .enable("false")) multiplexer_3 (
    .in0(divider_1_out), .in1(negator_3_out), .out(LO), .sel(xor_1_out));
  Negator #(.width(32)) negator_3 (.in(divider_1_out), .out(negator_3_out));
  // Probe on LO
  // Probe on HI

  // Notes on the sheet:
  //   Signed_Division
endmodule

module Register_File (
  input  [4:0] DA,
  input  [31:0] DI,
  input  Clk,
  input  Reset,
  input  R_W,
  input  [4:0] SA,
  input  [4:0] SB,
  input  PUSH,
  input  POP,
  input  EN_PC,
  input  Mult_or_Div,
  input  [31:0] Hi_Input,
  input  [31:0] Lo_Input,
  output [31:0] A,
  output [31:0] B,
  output [31:0] STACK_POINTER,
  output [31:0] Hi_Output,
  output [31:0] Lo_Output
);

  wire E01, E02, E03, E04, E05, E06, E07, E08, E09, E10, E11, E12, E13, E14, E15, E16, E17, E18, E19, E20,
       E21, E22, E23, E24, E25, E26, E27, E28, E29, E30, E31, L31, or_1_out, or_2_out;
  wire [31:0] adder_1_out, D00, D01, D02, D03, D04, D05, D06, D07, D08, D09, D10, D11, D12, D13, D14, D15,
       D16, D17, D18, D19, D20, D21, D22, D23, D24, D25, D26, D27, D28, D29, D30, INPUT, multiplexer_3_out,
       multiplexer_4_out, multiplexer_5_out, subtractor_1_out;

  Register #(.width(32)) register_1 (.D(DI), .en(1'b0), .Q(D00), .clk(Clk), .clr(Reset));
  Register #(.width(32)) register_2 (.D(DI), .en(E01), .Q(D01), .clk(Clk), .clr(Reset));
  Register #(.width(32)) register_3 (.D(DI), .en(E02), .Q(D02), .clk(Clk), .clr(Reset));
  Register #(.width(32)) register_4 (.D(DI), .en(E03), .Q(D03), .clk(Clk), .clr(Reset));
  Register #(.width(32)) register_5 (.D(DI), .en(E04), .Q(D04), .clk(Clk), .clr(Reset));
  Register #(.width(32)) register_6 (.D(DI), .en(E05), .Q(D05), .clk(Clk), .clr(Reset));
  Register #(.width(32)) register_7 (.D(DI), .en(E06), .Q(D06), .clk(Clk), .clr(Reset));
  Register #(.width(32)) register_8 (.D(DI), .en(E07), .Q(D07), .clk(Clk), .clr(Reset));
  Register #(.width(32)) register_9 (.D(DI), .en(E08), .Q(D08), .clk(Clk), .clr(Reset));
  Register #(.width(32)) register_10 (.D(DI), .en(E09), .Q(D09), .clk(Clk), .clr(Reset));
  Register #(.width(32)) register_11 (.D(DI), .en(E10), .Q(D10), .clk(Clk), .clr(Reset));
  Register #(.width(32)) register_12 (.D(DI), .en(E11), .Q(D11), .clk(Clk), .clr(Reset));
  Register #(.width(32)) register_13 (.D(DI), .en(E12), .Q(D12), .clk(Clk), .clr(Reset));
  Register #(.width(32)) register_14 (.D(DI), .en(E13), .Q(D13), .clk(Clk), .clr(Reset));
  Register #(.width(32)) register_15 (.D(DI), .en(E14), .Q(D14), .clk(Clk), .clr(Reset));
  Register #(.width(32)) register_16 (.D(DI), .en(E15), .Q(D15), .clk(Clk), .clr(Reset));
  Multiplexer #(.select(5), .width(32), .enable("false")) multiplexer_1 (
    .in0(D00), .in1(D01), .in2(D02), .in3(D03), .in4(D04), .in5(D05), .in6(D06), .in7(D07), .in8(D08),
    .in9(D09), .in10(D10), .in11(D11), .in12(D12), .in13(D13), .in14(D14), .in15(D15), .in16(D16),
    .in17(D17), .in18(D18), .in19(D19), .in20(D20), .in21(D21), .in22(D22), .in23(D23), .in24(D24),
    .in25(D25), .in26(D26), .in27(D27), .in28(D28), .in29(D29), .in30(D30), .in31(STACK_POINTER), .out(A),
    .sel(SA));
  Register #(.width(32)) Hi (.D(Hi_Input), .en(Mult_or_Div), .Q(Hi_Output), .clk(Clk));  // open: clr
  Register #(.width(32)) Lo (.D(Lo_Input), .en(Mult_or_Div), .Q(Lo_Output), .clk(Clk));  // open: clr
  Register #(.width(32)) register_17 (.D(DI), .en(E16), .Q(D16), .clk(Clk), .clr(Reset));
  Register #(.width(32)) register_18 (.D(DI), .en(E17), .Q(D17), .clk(Clk), .clr(Reset));
  Register #(.width(32)) register_19 (.D(DI), .en(E18), .Q(D18), .clk(Clk), .clr(Reset));
  Register #(.width(32)) register_20 (.D(DI), .en(E19), .Q(D19), .clk(Clk), .clr(Reset));
  Register #(.width(32)) register_21 (.D(DI), .en(E20), .Q(D20), .clk(Clk), .clr(Reset));
  Register #(.width(32)) register_22 (.D(DI), .en(E21), .Q(D21), .clk(Clk), .clr(Reset));
  Register #(.width(32)) register_23 (.D(DI), .en(E22), .Q(D22), .clk(Clk), .clr(Reset));
  Register #(.width(32)) register_24 (.D(DI), .en(E23), .Q(D23), .clk(Clk), .clr(Reset));
  Register #(.width(32)) register_25 (.D(DI), .en(E24), .Q(D24), .clk(Clk), .clr(Reset));
  Register #(.width(32)) register_26 (.D(DI), .en(E25), .Q(D25), .clk(Clk), .clr(Reset));
  Register #(.width(32)) register_27 (.D(DI), .en(E26), .Q(D26), .clk(Clk), .clr(Reset));
  Register #(.width(32)) register_28 (.D(DI), .en(E27), .Q(D27), .clk(Clk), .clr(Reset));
  Register #(.width(32)) register_29 (.D(DI), .en(E28), .Q(D28), .clk(Clk), .clr(Reset));
  Register #(.width(32)) register_30 (.D(DI), .en(E29), .Q(D29), .clk(Clk), .clr(Reset));
  Register #(.width(32)) register_31 (.D(DI), .en(E30), .Q(D30), .clk(Clk), .clr(Reset));
  Multiplexer #(.select(5), .width(32), .enable("false")) multiplexer_2 (
    .in0(D00), .in1(D01), .in2(D02), .in3(D03), .in4(D04), .in5(D05), .in6(D06), .in7(D07), .in8(D08),
    .in9(D09), .in10(D10), .in11(D11), .in12(D12), .in13(D13), .in14(D14), .in15(D15), .in16(D16),
    .in17(D17), .in18(D18), .in19(D19), .in20(D20), .in21(D21), .in22(D22), .in23(D23), .in24(D24),
    .in25(D25), .in26(D26), .in27(D27), .in28(D28), .in29(D29), .in30(D30), .in31(STACK_POINTER), .out(B),
    .sel(SB));
  Demultiplexer #(.select(5), .enable("false")) demultiplexer_1 (
    .out1(E01), .out2(E02), .out3(E03), .out4(E04), .out5(E05), .out6(E06), .out7(E07), .out8(E08),
    .out9(E09), .out10(E10), .out11(E11), .out12(E12), .out13(E13), .out14(E14), .out15(E15), .out16(E16),
    .out17(E17), .out18(E18), .out19(E19), .out20(E20), .out21(E21), .out22(E22), .out23(E23), .out24(E24),
    .out25(E25), .out26(E26), .out27(E27), .out28(E28), .out29(E29), .out30(E30), .out31(E31), .in(R_W),
    .sel(DA));  // open: out0
  Subtractor #(.width(32)) subtractor_1 (.a(STACK_POINTER), .b(32'h4), .out(subtractor_1_out));  // open: bin, bout
  Multiplexer #(.width(32), .enable("false")) multiplexer_3 (
    .in0(subtractor_1_out), .in1(adder_1_out), .out(multiplexer_3_out), .sel(POP));
  Multiplexer #(.width(32), .enable("false")) multiplexer_4 (
    .in0(multiplexer_3_out), .in1({32{1'b1}}), .out(multiplexer_4_out), .sel(Reset));
  Multiplexer #(.width(32), .enable("false")) multiplexer_5 (
    .in0(multiplexer_4_out), .in1(INPUT), .out(multiplexer_5_out), .sel(E31));
  or or_1 (or_1_out, Reset, E31, L31);
  Register #(.width(32)) register_32 (.D(multiplexer_5_out), .en(or_1_out), .Q(STACK_POINTER), .clk(Clk));  // open: clr
  Adder #(.width(32)) adder_1 (.a(STACK_POINTER), .b(32'h4), .out(adder_1_out));  // open: cin, cout
  or or_2 (or_2_out, PUSH, POP);
  and and_1 (L31, or_2_out, EN_PC);

  // Other names for the same wires on the sheet: C = Clk; D31[31:0] = STACK_POINTER; IN[31:0] = DI; R = Reset;
  //   WRITE = R_W

  // Notes on the sheet:
  //   Inputs
  //   Register File
  //   Outputs
endmodule

module REGISTER_FILE_INPUT (
  input  [6:0] KEYBOARD,
  input  [31:0] ALU,
  input  [31:0] RND,
  input  [31:0] MEMORY,
  input  [31:0] HIGH,
  input  [31:0] LOW,
  input  LW,
  input  POP,
  input  MFHI,
  input  MFLO,
  input  isKBD,
  input  isRND,
  output [31:0] Output
);

  wire [2:0] SELECTOR;

  or or_1 (SELECTOR[2], MFLO, isKBD, isRND);
  or or_2 (SELECTOR[1], POP, MFHI, isRND);
  or or_3 (SELECTOR[0], LW, MFHI, isKBD);
  // Probe on SELECTOR
  Multiplexer #(.select(3), .width(32), .enable("false")) multiplexer_1 (
    .in0(ALU), .in1(MEMORY), .in2(MEMORY), .in3(HIGH), .in4(LOW), .in5({{25{1'b0}}, KEYBOARD}), .in6(RND),
    .out(Output), .sel(SELECTOR));  // open: in7

  // Other names for the same wires on the sheet: KBD[6:0] = KEYBOARD

  // Notes on the sheet:
  //   Register File Input
  //   Esta circuito es el encargado de proporcionarle al Register File 
  //   el valor en memoria que queremos almacenar
endmodule

module Branch_Control (
  input  NOP,
  input  BEQ,
  input  [25:0] DEST,
  input  [31:0] RS,
  input  [31:0] RT,
  input  [31:0] PC,
  input  BNE,
  input  [15:0] OFFSET,
  input  BLEZ,
  input  BGTZ,
  input  BLTZ,
  input  JR,
  input  J,
  output [31:0] BC_OUT
);

  wire and_1_out, and_2_out, and_3_out, and_4_out, and_5_out, and_6_out, comparator_1_eq, not_1_out,
       or_1_out, RS__0, RS___0, RS____RT;
  wire [1:0] or_3_out;
  wire [31:0] PC_4, PC_4_4_OFFSET;
  wire [31:18] bit_extender_1_out;

  and and_1 (and_1_out, BEQ, RS____RT);
  and and_2 (and_2_out, ~RS____RT, BNE);  // AND_Gate
  and and_3 (and_3_out, BLEZ, RS___0);
  and and_4 (and_4_out, ~RS___0, BGTZ);  // AND_Gate
  and and_5 (and_5_out, BLTZ, RS__0);
  // Probe on {bit_extender_1_out, OFFSET, 2'b00}
  or or_1 (or_1_out, and_1_out, and_2_out, and_3_out, and_4_out, and_5_out);
  Adder #(.width(32)) adder_1 (.a(PC), .b(32'h4), .out(PC_4));  // open: cin, cout
  assign bit_extender_1_out = {{13{OFFSET[15]}}, OFFSET[15]};  // Bit_Extender bit_extender_1
  and and_6 (and_6_out, or_1_out, not_1_out);
  not not_1 (not_1_out, NOP);
  Adder #(.width(32)) adder_2 (
    .a(PC_4), .b({bit_extender_1_out, OFFSET, 2'b00}), .out(PC_4_4_OFFSET));  // open: cin, cout
  or or_2 (or_3_out[1], J, JR);
  or or_3 (or_3_out[0], and_6_out, JR);
  Comparator #(.width(32)) comparator_1 (.a(RS), .b({32{1'b0}}), .eq(comparator_1_eq), .lt(RS__0));  // open: gt
  Comparator #(.width(32)) comparator_2 (.a(RS), .b(RT), .eq(RS____RT));  // open: gt, lt
  // Probe on or_3_out
  or or_4 (RS___0, comparator_1_eq, RS__0);
  Multiplexer #(.select(2), .width(32), .enable("false")) multiplexer_1 (
    .in0(PC_4), .in1(PC_4_4_OFFSET), .in2({PC[31:28], DEST, 2'b00}), .in3(RS), .out(BC_OUT), .sel(or_3_out));
  // Probe on OFFSET

  // Other names for the same wires on the sheet: Jmp[31:2] = {PC[31:28], DEST}

  // Notes on the sheet:
  //   Branch Control
endmodule

module Instruction_Decoder (
  input  [31:0] Instruction,
  output [15:0] Constante,
  output [4:0] Rd,
  output [25:0] Destino_Salto,
  output [4:0] Rt,
  output [4:0] Rs,
  output ADD,
  output AND,
  output SLT,
  output NOP,
  output LW,
  output SUB,
  output OR,
  output SLTU,
  output BEQ,
  output SW,
  output MULT,
  output NOR,
  output SLTI,
  output BNE,
  output POP,
  output MULU,
  output XOR,
  output SLTIU,
  output BLEZ,
  output PUSH,
  output DIV,
  output ANDI,
  output BGTZ,
  output DIVU,
  output ORI,
  output MFHI,
  output BLTZ,
  output HALT,
  output ADDI,
  output XORI,
  output MFLO,
  output J,
  output TTY,
  output JR,
  output RND,
  output KBD
);

  wire _000000, _001010, _001100, _111111, comparator_11_eq, comparator_11_gt, comparator_12_eq,
       comparator_16_eq, comparator_17_eq, comparator_18_eq, comparator_19_eq, comparator_20_eq,
       comparator_21_eq, comparator_22_eq, comparator_23_eq, comparator_24_eq, comparator_25_eq,
       comparator_26_eq, comparator_27_eq, comparator_28_eq, comparator_29_eq, comparator_30_eq,
       comparator_31_eq, comparator_32_eq, comparator_33_eq, comparator_34_eq, comparator_35_eq,
       comparator_36_eq, comparator_37_eq, comparator_38_eq, not_1_out, not_2_out, not_3_out;

  Comparator #(.width(6)) comparator_1 (.a(Instruction[31:26]), .b({6{1'b0}}), .eq(_000000));  // open: gt, lt
  Comparator #(.width(6)) comparator_2 (.a(Instruction[31:26]), .b({6{1'b1}}), .eq(_111111));  // open: gt, lt
  Comparator #(.width(6)) comparator_3 (.a(Instruction[31:26]), .b(6'b001000), .eq(ADDI));  // open: gt, lt
  Comparator #(.width(6)) comparator_4 (.a(Instruction[31:26]), .b(6'b001010), .eq(_001010));  // open: gt, lt
  Comparator #(.width(6)) comparator_5 (.a(Instruction[31:26]), .b(6'b000100), .eq(BEQ));  // open: gt, lt
  Comparator #(.width(6)) comparator_6 (.a(Instruction[31:26]), .b(6'b001100), .eq(_001100));  // open: gt, lt
  Comparator #(.width(6)) comparator_7 (.a(Instruction[31:26]), .b(6'b000101), .eq(BNE));  // open: gt, lt
  Comparator #(.width(6)) comparator_8 (.a(Instruction[31:26]), .b(6'b000110), .eq(BLEZ));  // open: gt, lt
  Comparator #(.width(6)) comparator_9 (.a(Instruction[31:26]), .b(6'b100011), .eq(LW));  // open: gt, lt
  Comparator #(.width(6)) comparator_10 (.a(Instruction[31:26]), .b(6'b101011), .eq(SW));  // open: gt, lt
  Comparator #(.width(6)) comparator_11 (
    .a(Instruction[5:0]), .b({6{1'b0}}), .gt(comparator_11_gt), .eq(comparator_11_eq));  // open: lt
  Comparator #(.width(6)) comparator_12 (.a(Instruction[31:26]), .b(6'b111000), .eq(comparator_12_eq));  // open: gt, lt
  Comparator #(.width(6)) comparator_13 (.a(Instruction[31:26]), .b(6'b000001), .eq(BLTZ));  // open: gt, lt
  Comparator #(.width(6)) comparator_14 (.a(Instruction[31:26]), .b(6'b000010), .eq(J));  // open: gt, lt
  Comparator #(.width(6)) comparator_15 (.a(Instruction[31:26]), .b(6'b000111), .eq(BGTZ));  // open: gt, lt
  and and_1 (POP, comparator_11_eq, comparator_12_eq);
  and and_2 (PUSH, comparator_11_gt, comparator_12_eq);
  Comparator #(.width(6)) comparator_16 (.a(Instruction[5:0]), .b(6'b001011), .eq(comparator_16_eq));  // open: gt, lt
  and and_3 (SLTIU, _001100, comparator_16_eq);
  not not_1 (not_1_out, SLTIU);
  and and_4 (SLTI, not_1_out, _001100);
  Comparator #(.width(6)) comparator_17 (.a(Instruction[5:0]), .b({6{1'b1}}), .eq(comparator_17_eq));  // open: gt, lt
  Comparator #(.width(6)) comparator_18 (.a(Instruction[5:0]), .b(6'b000001), .eq(comparator_18_eq));  // open: gt, lt
  Comparator #(.width(6)) comparator_19 (.a(Instruction[5:0]), .b(6'b000010), .eq(comparator_19_eq));  // open: gt, lt
  Comparator #(.width(6)) comparator_20 (.a(Instruction[5:0]), .b(6'b000100), .eq(comparator_20_eq));  // open: gt, lt
  Comparator #(.width(6)) comparator_21 (.a(Instruction[5:0]), .b(6'b001101), .eq(comparator_21_eq));  // open: gt, lt
  Comparator #(.width(6)) comparator_22 (.a(Instruction[5:0]), .b(6'b001110), .eq(comparator_22_eq));  // open: gt, lt
  and and_5 (HALT, _111111, comparator_17_eq);
  and and_6 (TTY, _111111, comparator_18_eq);
  and and_7 (RND, _111111, comparator_19_eq);
  and and_8 (KBD, _111111, comparator_20_eq);
  and and_9 (ORI, _001010, comparator_21_eq);
  and and_10 (XORI, _001010, comparator_22_eq);
  not not_2 (not_2_out, ORI);
  not not_3 (not_3_out, XORI);
  and and_11 (ANDI, not_2_out, not_3_out, _001010);
  and and_12 (NOP, _000000, comparator_23_eq);
  Comparator #(.width(6)) comparator_23 (.a(Instruction[5:0]), .b({6{1'b0}}), .eq(comparator_23_eq));  // open: gt, lt
  and and_13 (ADD, _000000, comparator_24_eq);
  Comparator #(.width(6)) comparator_24 (.a(Instruction[5:0]), .b(6'b100000), .eq(comparator_24_eq));  // open: gt, lt
  and and_14 (SUB, _000000, comparator_25_eq);
  Comparator #(.width(6)) comparator_25 (.a(Instruction[5:0]), .b(6'b100010), .eq(comparator_25_eq));  // open: gt, lt
  and and_15 (MULT, _000000, comparator_26_eq);
  Comparator #(.width(6)) comparator_26 (.a(Instruction[5:0]), .b(6'b011000), .eq(comparator_26_eq));  // open: gt, lt
  and and_16 (MULU, _000000, comparator_27_eq);
  Comparator #(.width(6)) comparator_27 (.a(Instruction[5:0]), .b(6'b011001), .eq(comparator_27_eq));  // open: gt, lt
  and and_17 (DIV, _000000, comparator_28_eq);
  Comparator #(.width(6)) comparator_28 (.a(Instruction[5:0]), .b(6'b011010), .eq(comparator_28_eq));  // open: gt, lt
  and and_18 (DIVU, _000000, comparator_29_eq);
  Comparator #(.width(6)) comparator_29 (.a(Instruction[5:0]), .b(6'b011011), .eq(comparator_29_eq));  // open: gt, lt
  and and_19 (SLT, _000000, comparator_30_eq);
  Comparator #(.width(6)) comparator_30 (.a(Instruction[5:0]), .b(6'b101010), .eq(comparator_30_eq));  // open: gt, lt
  and and_20 (SLTU, _000000, comparator_31_eq);
  Comparator #(.width(6)) comparator_31 (.a(Instruction[5:0]), .b(6'b101011), .eq(comparator_31_eq));  // open: gt, lt
  and and_21 (AND, _000000, comparator_32_eq);
  Comparator #(.width(6)) comparator_32 (.a(Instruction[5:0]), .b(6'b100100), .eq(comparator_32_eq));  // open: gt, lt
  and and_22 (OR, _000000, comparator_33_eq);
  Comparator #(.width(6)) comparator_33 (.a(Instruction[5:0]), .b(6'b100101), .eq(comparator_33_eq));  // open: gt, lt
  and and_23 (NOR, _000000, comparator_34_eq);
  Comparator #(.width(6)) comparator_34 (.a(Instruction[5:0]), .b(6'b100111), .eq(comparator_34_eq));  // open: gt, lt
  and and_24 (XOR, _000000, comparator_35_eq);
  Comparator #(.width(6)) comparator_35 (.a(Instruction[5:0]), .b(6'b101000), .eq(comparator_35_eq));  // open: gt, lt
  and and_25 (JR, _000000, comparator_36_eq);
  Comparator #(.width(6)) comparator_36 (.a(Instruction[5:0]), .b(6'b001000), .eq(comparator_36_eq));  // open: gt, lt
  and and_26 (MFHI, _000000, comparator_37_eq);
  Comparator #(.width(6)) comparator_37 (.a(Instruction[5:0]), .b(6'b010000), .eq(comparator_37_eq));  // open: gt, lt
  and and_27 (MFLO, _000000, comparator_38_eq);
  Comparator #(.width(6)) comparator_38 (.a(Instruction[5:0]), .b(6'b010010), .eq(comparator_38_eq));  // open: gt, lt

  assign Constante = Instruction[15:0];
  assign Destino_Salto = Instruction[25:0];
  assign Rd = Instruction[15:11];
  assign Rs = Instruction[25:21];
  assign Rt = Instruction[20:16];

  // Other names for the same wires on the sheet: FUNC_CODE[5:0] = Instruction[5:0]; x[4:0] = Instruction[10:6];
  //   OP_CODE[5:0] = Instruction[31:26]

  // Notes on the sheet:
  //   Instruction Decoder
  //   Output_Zone
endmodule

module Memory_Address (
  input  [31:0] ALU,
  input  [31:0] PC,
  input  [31:0] SP,
  input  POP,
  input  PUSH,
  input  LW,
  input  SW,
  input  PC_ADDRESS,
  output [31:0] MEMORY
);

  wire [1:0] or_2_out;
  wire [31:0] multiplexer_1_out, subtractor_1_out;

  Subtractor #(.width(32)) subtractor_1 (.a(SP), .b(32'h4), .out(subtractor_1_out));  // open: bin, bout
  Multiplexer #(.width(32), .enable("false")) multiplexer_1 (
    .in0(SP), .in1(subtractor_1_out), .out(multiplexer_1_out), .sel(PUSH));
  Multiplexer #(.select(2), .width(32), .enable("false")) multiplexer_2 (
    .in0(PC), .in1(ALU), .in2(multiplexer_1_out), .in3(PC), .out(MEMORY), .sel(or_2_out));
  or or_1 (or_2_out[1], PUSH, POP, PC_ADDRESS);
  or or_2 (or_2_out[0], PC_ADDRESS, LW, SW);

  // Notes on the sheet:
  //   Memory_Address
endmodule

module Program_Counter (
  input  [31:0] INPUT,
  input  RESET,
  input  ENABLE,
  input  CLK,
  output [31:0] PC_OUTPUT
);

  Register #(.width(32)) register_1 (.D(INPUT), .en(ENABLE), .Q(PC_OUTPUT), .clk(CLK), .clr(RESET));

  // Notes on the sheet:
  //   Program Counter
endmodule

module COUNTER (
  input  [3:0] TIME,
  input  START,
  input  CLK,
  input  RESET,
  output OUT
);

  wire [3:0] counter_1_q;

  Counter #(.width(4), .max('hf)) counter_1 (
    .count(START), .Q(counter_1_q), .clk(CLK), .clr(RESET));  // open: load, D, carry
  Comparator #(.width(4)) comparator_1 (.a(TIME), .b(counter_1_q), .eq(OUT));  // open: gt, lt

  // Notes on the sheet:
  //   COUNTER
endmodule
